# Fritzing sketch breadbrd1 (saved by Fritzing 0.8.7b)
breadboards: 1

parts:
  Part1 = Photon
  J1 = Basic Force Sensing Resistor (FSR) [package=THT]
  R1 = Resistor [tolerance=±5% resistance=220 package=THT]
  J2 = Piezo Speaker
  LED1 = LED - 5mm [color="Red (633nm)" package="5 mm [THT]"]
  LED2 = LED - 5mm [color="Red (633nm)" package="5 mm [THT]"]
  LED3 = LED - 5mm [color="Red (633nm)" package="5 mm [THT]"]
  R2 = Resistor [tolerance=±5% resistance=220 package=THT]
  R3 = Resistor [tolerance=±5% resistance=220 package=THT]
  R4 = Resistor [tolerance=±5% resistance=220 package=THT]

nets:
  N1: Part1.A5, J1.pin_0, R1.Pin_0
  N2: Part1.GND, R1.Pin_1, J2.pin1, LED1.cathode, LED2.cathode, LED3.cathode
  N3: Part1.D1, R4.Pin_0
  N4: Part1.D2, R3.Pin_0
  N5: Part1.D3, R2.Pin_0
  N6: Part1.D4, J2.pin2
  N7: Part1.3V3, J1.pin_1
  N8: LED1.anode, R2.Pin_1
  N9: LED2.anode, R3.Pin_1
  N10: LED3.anode, R4.Pin_1
